// Digital circuit MIni_D_CPU_2.dig as structural Verilog
module MIni_D_CPU_2 (
  input  in_1,
  input  in_2,
  input  in_3,
  input  in_4,
  input  in_5,
  input  in_6,
  input  in_7,
  input  in_8,
  input  in_9,
  input  in_10,
  input  in_11,
  input  in_12,
  input  in_13,
  input  in_15,
  input  in_16,
  input  in_17,
  input  clk,
  input  in_28,
  input  in_29,
  output out_14,
  output LP,
  output _320,
  output _268,
  output _266,
  output _136,
  output MCC,
  output _292,
  output _262,
  output RCO
);

  wire _134_pin11, _134_pin12, _134_pin13, _74138_1_pin9, _74138_1_pin10, _74138_1_pin11, _74138_1_pin12,
       _74138_1_pin13, _74138_1_pin14, _74138_1_pin15, _74161_1_pin15, _74540_2_pin11, _74540_2_pin12,
       _74540_2_pin13, _74540_2_pin14, A, A1, A1in, A1out, A2, A2in, A2out, A3, A3in, A3out, ADDin, ALU_OP,
       AMPC1, AMPC2, AMPC3, AMPC4, AMPC5, AMPC6, AMPC7, AMPC8, AMPCR_OUT1, AMPCR_OUT2, AMPCR_OUT3,
       AMPCR_OUT4, AMPCR_OUT5, AMPCR_OUT6, AMPCR_OUT7, AMPCR_OUT8, and_1_out, and_2_out, and_3_out,
       and_4_out, and_5_out, and_6_out, and_7_out, and_8_out, B, B3, Bin, Bout, CARRYout, Cin, CONDIT, COUNT,
       d_ff_as_2_q, d_ff_as_3_q, d_ff_as_4_q, d_ff_as_5_q, DEVin, DEVout, GCLK, H1, H2, H3, H4, H5, H6, H7,
       H8, H9, I1, I2, I3, I4, I5, I6, I7, I8, I9, JUMP, JUMP_F, JUMP_T, LC1, LC1_CLK, LC2, LC2_CLK, LC3,
       LC3_CLK, LC4, LC4_CLK, LCout, LD_AMPC, LIT_AMPCR, LIT_B, LIT_JUMP, nand_9_out, nand_14_out,
       nand_15_out, nand_16_out, nand_17_out, nand_18_out, nand_19_out, nand_20_out, nand_21_out,
       nand_22_out, nand_23_out, nand_24_out, nand_25_out, nand_26_out, nand_27_out, nand_28_out,
       nand_29_out, nand_30_out, nand_31_out, nand_32_out, nand_33_out, nand_34_out, nand_35_out,
       nand_36_out, nand_37_out, nand_44_out, nand_45_out, nand_46_out, nand_47_out, nand_61_out,
       nand_62_out, nand_63_out, nand_64_out, nand_65_out, nand_66_out, nand_67_out, nand_68_out,
       nand_73_out, nand_74_out, nand_77_out, nand_78_out, nand_79_out, nand_83_out, nand_84_out,
       nand_85_out, nand_86_out, nand_87_out, nand_88_out, nand_89_out, nand_90_out, nand_91_out,
       nand_92_out, nH2, nI1, nI5, nI6, nLD_MPCR, nLDB, nN1, nN2, nN3, nN4, nN5, nN6, nN7, nN8, nN9, nN10,
       nN11, nN12, nor_3_out, nor_9_out, nor_13_out, not_5_out, not_6_out, not_7_out, not_9_out, not_10_out,
       not_11_out, not_12_out, not_13_out, not_14_out, not_15_out, not_16_out, not_19_out, not_20_out,
       not_21_out, not_22_out, not_23_out, not_24_out, not_25_out, not_26_out, not_27_out, not_28_out,
       not_29_out, not_30_out, not_31_out, not_32_out, not_33_out, not_34_out, not_35_out, not_36_out,
       not_37_out, not_38_out, not_39_out, not_40_out, not_41_out, not_42_out, not_43_out, not_44_out,
       not_45_out, not_46_out, not_47_out, not_48_out, not_49_out, not_50_out, not_51_out, not_52_out,
       not_53_out, not_54_out, not_55_out, not_56_out, not_58_out, not_60_out, not_61_out, not_62_out, nRES,
       or_1_out, QA, RA0, RA1, RA2, RA3, RA4, RA5, RA6, RA7, RST, SAVE, SAVE_F, SAVE_T, SERIN, SKIP, SKIP_F,
       SKIP_T, STEP, STEP_F, STEP_T, SUMout, undriven, Xin, xnor_1_out, xnor_2_out, Yin;
  wire [3:0] U5_pin3, U6_pin3, U7_2_pin3;
  wire [3:1] U5_pin10, U6_pin10, U7_2_pin10;

  nand nand_1 (H1, in_9, in_8, in_7);
  nand nand_2 (H2, nN11, in_7);
  nor nor_1 (H3, nN11, in_9);
  nand nand_3 (H4, nN11, in_2, in_1, in_9);
  nor nor_2 (H5, nN11, in_2);
  nor nor_3 (nor_3_out, in_3, nN8);
  nand nand_4 (H8, nH2, H5);
  nand nand_5 (H9, nor_3_out, nH2);
  nand nand_6 (A, H9, H7);
  nand nand_7 (B, H7, H8);
  _74157 _74157_1 (
    .pin2(in_12), .pin3(RA0), .pin4(AMPC1), .pin5(in_11), .pin6(RA1), .pin7(AMPC2), .pin8(1'b0),
    .pin9(AMPC3), .pin10(RA2), .pin11(in_10), .pin12(AMPC4), .pin13(RA3), .pin14(in_6), .pin16(1'b1));  // open: pin1, pin15
  _74157 _74157_2 (
    .pin2(in_5), .pin3(RA4), .pin4(AMPC5), .pin5(in_4), .pin6(RA5), .pin7(AMPC6), .pin8(1'b0), .pin9(AMPC7),
    .pin10(RA6), .pin11(in_3), .pin12(AMPC8), .pin13(RA7), .pin14(in_2), .pin16(1'b1));  // open: pin1, pin15
  not not_1 (nH2, H2);
  nand nand_8 (I1, _266, _268, in_16);
  nand nand_9 (nand_9_out, _266, _268);
  nand nand_10 (I2, nand_9_out, in_3, in_2);
  nand nand_11 (I3, in_16, nH2);
  nand nand_12 (I4, nI1, nH2);
  nor nor_4 (I5, H1, B3);
  nor nor_5 (I6, B3, in_7);
  nor nor_6 (I9, I3, H4);
  nor nor_7 (I7, H1, _320);
  nand nand_13 (I8, nI1, H3, in_1, in_7);
  not not_2 (nI1, I1);
  not not_3 (nI5, I5);
  not not_4 (nI6, I6);
  not not_5 (not_5_out, not_6_out);
  not not_6 (not_6_out, LD_AMPC);
  nand nand_14 (nand_14_out, SERIN, not_6_out);
  nand nand_15 (nand_15_out, AMPC8, not_5_out);
  nand nand_16 (nand_16_out, AMPCR_OUT8, not_6_out);
  nand nand_17 (nand_17_out, AMPC7, not_5_out);
  nand nand_18 (nand_18_out, AMPCR_OUT7, not_6_out);
  nand nand_19 (nand_19_out, AMPC6, not_5_out);
  nand nand_20 (nand_20_out, AMPCR_OUT6, not_6_out);
  nand nand_21 (nand_21_out, AMPC5, not_5_out);
  nand nand_22 (nand_22_out, AMPCR_OUT5, not_6_out);
  nand nand_23 (nand_23_out, AMPC4, not_5_out);
  nand nand_24 (nand_24_out, AMPCR_OUT4, not_6_out);
  nand nand_25 (nand_25_out, AMPC3, not_5_out);
  nand nand_26 (nand_26_out, AMPCR_OUT3, not_6_out);
  nand nand_27 (nand_27_out, AMPC2, not_5_out);
  nand nand_28 (nand_28_out, AMPCR_OUT2, not_6_out);
  nand nand_29 (nand_29_out, AMPC1, not_5_out);
  and and_1 (and_1_out, not_6_out, in_16);
  nand nand_30 (nand_30_out, nand_14_out, nand_15_out);
  nand nand_31 (nand_31_out, nand_16_out, nand_17_out);
  nand nand_32 (nand_32_out, nand_18_out, nand_19_out);
  nand nand_33 (nand_33_out, nand_20_out, nand_21_out);
  nand nand_34 (nand_34_out, nand_22_out, nand_23_out);
  nand nand_35 (nand_35_out, nand_24_out, nand_25_out);
  nand nand_36 (nand_36_out, nand_26_out, nand_27_out);
  nand nand_37 (nand_37_out, nand_28_out, nand_29_out);
  or or_1 (or_1_out, LD_AMPC, and_1_out);
  not not_7 (not_7_out, or_1_out);
  // Not not_8 has open pins: in=LP, out=open
  not not_9 (not_9_out, nand_30_out);
  not not_10 (not_10_out, nand_31_out);
  not not_11 (not_11_out, nand_32_out);
  not not_12 (not_12_out, nand_33_out);
  not not_13 (not_13_out, nand_34_out);
  not not_14 (not_14_out, nand_35_out);
  not not_15 (not_15_out, nand_36_out);
  not not_16 (not_16_out, nand_37_out);
  nand nand_38 (COUNT, clk, LP);
  RS_FF rs_ff_1 (.S(nand_30_out), .C(not_7_out), .R(not_9_out), .Q(AMPCR_OUT8));  // open: nQ
  RS_FF rs_ff_2 (.S(nand_31_out), .C(not_7_out), .R(not_10_out), .Q(AMPCR_OUT7));  // open: nQ
  RS_FF rs_ff_3 (.S(nand_32_out), .C(not_7_out), .R(not_11_out), .Q(AMPCR_OUT6));  // open: nQ
  RS_FF rs_ff_4 (.S(nand_33_out), .C(not_7_out), .R(not_12_out), .Q(AMPCR_OUT5));  // open: nQ
  RS_FF rs_ff_5 (.S(nand_34_out), .C(not_7_out), .R(not_13_out), .Q(AMPCR_OUT4));  // open: nQ
  RS_FF rs_ff_6 (.S(nand_35_out), .C(not_7_out), .R(not_14_out), .Q(AMPCR_OUT3));  // open: nQ
  RS_FF rs_ff_7 (.S(nand_36_out), .C(not_7_out), .R(not_15_out), .Q(AMPCR_OUT2));  // open: nQ
  RS_FF rs_ff_8 (.S(nand_37_out), .C(not_7_out), .R(not_16_out), .Q(AMPCR_OUT1));  // open: nQ
  nand nand_39 (B3, _134_pin11, MCC);
  not not_17 (_136, COUNT);
  nor nor_8 (_266, _134_pin13, _134_pin12);
  _74161 _134 (
    .pin1(B3), .pin2(COUNT), .pin3(1'b0), .pin4(1'b0), .pin5(1'b0), .pin6(1'b0), .pin7(1'b1), .pin8(1'b0),
    .pin9(1'b1), .pin10(1'b1), .pin11(_134_pin11), .pin12(_134_pin12), .pin13(_134_pin13), .pin14(QA),
    .pin16(1'b1));  // open: pin15
  nand nand_40 (LP, QA, _134_pin13, _134_pin12);
  nand nand_41 (_320, QA, _266, _136);
  not not_18 (_268, QA);
  _74161 _74161_1 (
    .pin1(RST), .pin2(in_16), .pin3(AMPCR_OUT1), .pin4(AMPCR_OUT2), .pin5(AMPCR_OUT3), .pin6(AMPCR_OUT4),
    .pin7(1'b1), .pin8(1'b0), .pin9(nLD_MPCR), .pin10(1'b1), .pin11(RA3), .pin12(RA2), .pin13(RA1),
    .pin14(RA0), .pin15(_74161_1_pin15), .pin16(1'b1));
  _74161 _74161_2 (
    .pin1(RST), .pin2(in_16), .pin3(AMPCR_OUT5), .pin4(AMPCR_OUT6), .pin5(AMPCR_OUT7), .pin6(AMPCR_OUT8),
    .pin7(1'b1), .pin8(1'b0), .pin9(nLD_MPCR), .pin10(_74161_1_pin15), .pin11(RA7), .pin12(RA6), .pin13(RA5),
    .pin14(RA4), .pin16(1'b1));  // open: pin15
  // _27C1024 _27c1024_1: pin names not known; wires that end beside it: 1'b1, 1'b0, in_7, in_8, in_9, in_1, 1'b0, in_2, in_3, in_4, in_5, in_6, 1'b1, 1'b0, 1'b0, 1'b0, 1'b0, 1'b0, 1'b0, 1'b0
  nand nand_42 (_292, _268, _266, _136);
  nand nand_43 (_262, _268, _266);
  not not_19 (not_19_out, in_12);
  not not_20 (not_20_out, in_11);
  not not_21 (not_21_out, in_9);
  not not_22 (not_22_out, in_1);
  not not_23 (not_23_out, in_9);
  not not_24 (not_24_out, in_1);
  not not_25 (not_25_out, in_5);
  not not_26 (not_26_out, in_6);
  not not_27 (not_27_out, in_15);
  not not_28 (not_28_out, in_15);
  not not_29 (not_29_out, LCout);
  not not_30 (not_30_out, not_19_out);
  not not_31 (not_31_out, not_20_out);
  not not_32 (not_32_out, not_21_out);
  not not_33 (not_33_out, not_22_out);
  not not_34 (not_34_out, not_23_out);
  not not_35 (not_35_out, not_24_out);
  not not_36 (not_36_out, not_25_out);
  not not_37 (not_37_out, not_26_out);
  nand nand_44 (nand_44_out, not_19_out, not_20_out, 1'b0);
  nand nand_45 (nand_45_out, not_19_out, not_31_out, A1out);
  nand nand_46 (nand_46_out, not_30_out, not_20_out, A2out);
  nand nand_47 (nand_47_out, not_30_out, not_30_out, A3out);
  nand nand_48 (A1in, not_21_out, not_22_out, not_27_out);
  nand nand_49 (A2in, not_21_out, not_33_out, not_27_out);
  nand nand_50 (A3in, not_32_out, not_22_out, not_27_out);
  nand nand_51 (Bin, not_32_out, not_32_out, not_27_out);
  nand nand_52 (A1, not_23_out, not_24_out, not_28_out);
  nand nand_53 (A2, not_23_out, not_35_out, not_28_out);
  nand nand_54 (A3, not_34_out, not_24_out, not_28_out);
  nand nand_55 (B, not_34_out, not_34_out, not_28_out);
  nand nand_56 (LC1, not_25_out, not_26_out, not_29_out);
  nand nand_57 (LC2, not_25_out, not_37_out, not_29_out);
  nand nand_58 (LC3, not_36_out, not_26_out, not_29_out);
  nand nand_59 (LC4, not_36_out, not_36_out, not_29_out);
  _74540 _74540_1 (
    .pin1(1'b0), .pin2(in_12), .pin3(in_11), .pin4(in_10), .pin5(in_6), .pin6(in_5), .pin7(in_4),
    .pin8(in_3), .pin9(in_2), .pin10(1'b0), .pin11(nN8), .pin12(nN7), .pin13(nN6), .pin14(nN5), .pin15(nN4),
    .pin16(nN3), .pin17(nN2), .pin18(nN1), .pin19(1'b0), .pin20(1'b1));
  _74540 _74540_2 (
    .pin1(1'b0), .pin2(in_1), .pin3(in_9), .pin4(in_8), .pin5(in_7), .pin6(1'b0), .pin7(1'b0), .pin8(1'b0),
    .pin9(1'b0), .pin10(1'b0), .pin11(_74540_2_pin11), .pin12(_74540_2_pin12), .pin13(_74540_2_pin13),
    .pin14(_74540_2_pin14), .pin15(nN12), .pin16(nN11), .pin17(nN10), .pin18(nN9), .pin19(1'b0), .pin20(1'b1));
  nand nand_60 (Xin, nand_44_out, nand_45_out, nand_46_out, nand_47_out);
  Seven_Seg_Hex seven_seg_hex_1 (.d(U5_pin3), .dp(1'b0));
  _74164 U5 (
    .pin1(A1in), .pin2(A1out), .pin3(U5_pin3[3]), .pin4(U5_pin3[2]), .pin5(U5_pin3[1]), .pin6(U5_pin3[0]),
    .pin7(1'b0), .pin8(in_16), .pin9(nRES), .pin10(U5_pin10[3]), .pin11(U5_pin10[2]), .pin12(U5_pin10[1]),
    .pin13(A1out), .pin14(1'b1));
  Seven_Seg_Hex seven_seg_hex_2 (.d({U5_pin10, A1out}), .dp(1'b0));
  D_FF_AS d_ff_as_1 (.Set(~1'b1));  // open: D, C, Clr, Q, nQ
  not not_38 (not_38_out, in_28);
  not not_39 (not_39_out, in_29);
  not not_40 (not_40_out, in_5);
  not not_41 (not_41_out, in_6);
  not not_42 (not_42_out, not_38_out);
  not not_43 (not_43_out, not_39_out);
  not not_44 (not_44_out, LCout);
  not not_45 (not_45_out, not_40_out);
  not not_46 (not_46_out, not_41_out);
  _74165 U8 (
    .pin1(nLDB), .pin2(GCLK), .pin3(in_6), .pin4(in_10), .pin5(in_11), .pin6(in_12), .pin8(1'b0),
    .pin9(DEVout), .pin10(DEVin), .pin11(in_2), .pin12(in_3), .pin13(in_4), .pin14(in_5), .pin15(1'b0),
    .pin16(1'b1));  // open: pin7
  _74165 U7 (
    .pin1(nLDB), .pin2(GCLK), .pin3(in_6), .pin4(in_10), .pin5(in_11), .pin6(in_12), .pin8(1'b0),
    .pin9(Bout), .pin10(Bin), .pin11(in_2), .pin12(in_3), .pin13(in_4), .pin14(in_5), .pin15(1'b0),
    .pin16(1'b1));  // open: pin7
  D_FF_AS d_ff_as_2 (.Set(~1'b1), .Clr(~undriven), .Q(d_ff_as_2_q));  // open: D, C, nQ
  nand nand_61 (nand_61_out, not_38_out, not_39_out, in_3);
  nand nand_62 (nand_62_out, not_38_out, not_43_out, in_2);
  nand nand_63 (nand_63_out, not_42_out, not_39_out, nN11);
  nand nand_64 (nand_64_out, not_42_out, not_42_out, 1'b0);
  nand nand_65 (nand_65_out, not_38_out, not_39_out, in_4);
  nand nand_66 (nand_66_out, not_38_out, not_43_out, in_2);
  nand nand_67 (nand_67_out, not_42_out, not_39_out, in_7);
  nand nand_68 (nand_68_out, not_42_out, not_42_out, 1'b0);
  D_FF_AS d_ff_as_3 (.Set(~1'b1), .D(LC1), .C(LC1_CLK), .Clr(~LC1), .Q(d_ff_as_3_q));  // open: nQ
  nand nand_69 (LC1_CLK, not_40_out, not_41_out, not_44_out);
  nand nand_70 (LC2_CLK, not_40_out, not_46_out, not_44_out);
  nand nand_71 (LC3_CLK, not_45_out, not_41_out, not_44_out);
  nand nand_72 (LC4_CLK, not_45_out, not_45_out, not_44_out);
  Seven_Seg_Hex seven_seg_hex_3 (.d(U6_pin3), .dp(1'b0));
  _74164 U6 (
    .pin1(A2in), .pin2(A2out), .pin3(U6_pin3[3]), .pin4(U6_pin3[2]), .pin5(U6_pin3[1]), .pin6(U6_pin3[0]),
    .pin7(1'b0), .pin8(in_16), .pin9(nRES), .pin10(U6_pin10[3]), .pin11(U6_pin10[2]), .pin12(U6_pin10[1]),
    .pin13(A2out), .pin14(1'b1));
  nand nand_73 (nand_73_out, nand_61_out, nand_62_out, nand_63_out, nand_64_out);
  nand nand_74 (nand_74_out, nand_65_out, nand_66_out, nand_67_out, nand_68_out);
  // NAnd nand_75 is placed but not wired
  // NAnd nand_76 is placed but not wired
  Seven_Seg_Hex seven_seg_hex_4 (.d({U6_pin10, A2out}), .dp(1'b0));
  D_FF_AS d_ff_as_4 (.Set(~1'b1), .D(LC2), .C(LC2_CLK), .Clr(~LC2), .Q(d_ff_as_4_q));  // open: nQ
  _74139 _74139_1 (
    .pin1(1'b0), .pin2(1'b0), .pin3(1'b0), .pin8(1'b0), .pin9(LIT_B), .pin10(ALU_OP), .pin11(LIT_JUMP),
    .pin12(LIT_AMPCR), .pin13(in_7), .pin14(in_8), .pin15(1'b0), .pin16(1'b1));  // open: pin4, pin5, pin6, pin7
  not not_47 (not_47_out, nand_73_out);
  not not_48 (not_48_out, nand_74_out);
  D_FF_AS d_ff_as_5 (.Set(~1'b1), .D(LC3), .C(LC3_CLK), .Clr(~LC3), .Q(d_ff_as_5_q));  // open: nQ
  not not_49 (not_49_out, ALU_OP);
  not not_50 (not_50_out, Yin);
  not not_51 (not_51_out, Xin);
  nand nand_77 (nand_77_out, Yin, Xin);
  not not_52 (not_52_out, Cin);
  nand nand_78 (nand_78_out, in_4, I3);
  nand nand_79 (nand_79_out, nN6, I3);
  nand nand_80 (I3, in_16, not_49_out);
  or or_2 (JUMP, JUMP_F, JUMP_T);
  or or_3 (STEP, STEP_F, STEP_T);
  or or_4 (SKIP, SKIP_F, SKIP_T);
  or or_5 (SAVE, SAVE_F, SAVE_T);
  Seven_Seg_Hex seven_seg_hex_5 (.d(U7_2_pin3), .dp(1'b0));
  _74164 U7_2 (
    .pin1(A3in), .pin2(A3out), .pin3(U7_2_pin3[3]), .pin4(U7_2_pin3[2]), .pin5(U7_2_pin3[1]),
    .pin6(U7_2_pin3[0]), .pin7(1'b0), .pin8(in_16), .pin9(nRES), .pin10(U7_2_pin10[3]),
    .pin11(U7_2_pin10[2]), .pin12(U7_2_pin10[1]), .pin13(A3out), .pin14(1'b1));
  nor nor_9 (nor_9_out, H4, in_6);
  Seven_Seg_Hex seven_seg_hex_6 (.d({U7_2_pin10, A3out}), .dp(1'b0));
  not not_53 (not_53_out, in_8);
  xnor xnor_1 (xnor_1_out, not_50_out, not_51_out);
  and and_2 (and_2_out, not_50_out, not_51_out);
  not not_54 (not_54_out, nand_77_out);
  nand nand_81 (H4, in_2, in_1, in_9, not_53_out);
  _74138 _74138_1 (
    .pin1(in_9), .pin2(in_8), .pin3(in_7), .pin7(CONDIT), .pin8(1'b0), .pin9(_74138_1_pin9),
    .pin10(_74138_1_pin10), .pin11(_74138_1_pin11), .pin12(_74138_1_pin12), .pin13(_74138_1_pin13),
    .pin14(_74138_1_pin14), .pin15(_74138_1_pin15), .pin16(1'b1));  // open: pin4, pin5, pin6
  _74139 _74139_2 (
    .pin1(CONDIT), .pin2(in_4), .pin3(in_3), .pin4(JUMP_T), .pin5(STEP_T), .pin6(SKIP_T), .pin7(SAVE_T),
    .pin8(1'b0), .pin9(SAVE_F), .pin10(SKIP_F), .pin11(STEP_F), .pin12(JUMP_F), .pin13(in_1), .pin14(in_2),
    .pin15(CONDIT), .pin16(1'b1));
  and and_3 (and_3_out, nor_9_out, in_17, in_5);
  and and_4 (and_4_out, in_5, Bout, in_6);
  and and_5 (and_5_out, nN5, not_55_out);
  not not_55 (not_55_out, Bout);
  xnor xnor_2 (xnor_2_out, xnor_1_out, not_52_out);
  nor nor_10 (CARRYout, and_2_out, not_54_out);
  not not_56 (not_56_out, CARRYout);
  nor nor_11 (ADDin, and_3_out, and_4_out, and_5_out);
  Seven_Seg_Hex seven_seg_hex_7 (.d({in_2, in_3, in_4, in_5}), .dp(1'b0));
  not not_57 (SUMout, xnor_2_out);
  nor nor_12 (H6, in_1, in_9);
  nand nand_82 (H7, H6, in_8, in_7);
  nand nand_83 (nand_83_out, SUMout, nN3);
  nand nand_84 (nand_84_out, nN4, not_56_out, in_11);
  nand nand_85 (nand_85_out, CARRYout, in_6, in_6);
  Seven_Seg_Hex seven_seg_hex_8 (.d({in_6, in_10, in_11, in_12}), .dp(1'b0));
  nor nor_13 (nor_13_out, nand_83_out, nand_84_out, nand_85_out);
  not not_58 (not_58_out, I3);
  nand nand_86 (nand_86_out, in_6, nN5);
  // Not not_59 has open pins: in=1'b0, out=open
  nand nand_87 (nand_87_out, I3, in_4);
  nand nand_88 (nand_88_out, I3, nN6);
  nand nand_89 (nand_89_out, not_58_out, nN3, nand_86_out);
  nand nand_90 (nand_90_out, in_3, nN8);
  not not_60 (not_60_out, H7);
  not not_61 (not_61_out, 1'b0);
  nand nand_91 (nand_91_out, DEVout, not_60_out);
  nand nand_92 (nand_92_out, H7, nor_13_out);
  not not_62 (not_62_out, 1'b0);
  and and_6 (and_6_out, not_62_out, nand_90_out, 1'b0);
  and and_7 (and_7_out, nN8, in_13);  // open: In_3
  buf and_8 (and_8_out, not_61_out);  // And open: In_1
  nand nand_93 (out_14, nand_91_out, nand_92_out);
  D_FF_AS d_ff_as_6 (.Set(~nand_87_out), .D(CARRYout), .C(nand_89_out), .Clr(~nand_88_out), .Q(Cin));  // open: nQ
  nor nor_14 (Bin, and_6_out, and_7_out, and_8_out);

  assign RCO = LP;

  // Other names for the same wires on the sheet: B1 = _320; B2 = _268; B4 = _266; C1 = in_17; CLK_t = in_16;
  //   CLOCK_IN = clk; CO = _136; DATA_IN = in_13; DATA_OUT = out_14; CLR = B3; DEVload = B3; H10 = A; H11 = B;
  //   N1 = in_12; N2 = in_11; N3 = in_10; N4 = in_6; N5 = in_5; N6 = in_4; N7 = in_3; N8 = in_2; N9 = in_1;
  //   N10 = in_9; N11 = in_8; N12 = in_7; S1 = in_29; S2 = in_28; Xout = in_15

  // Notes on the sheet:
  //   ROM AMPCR MPCR
  //   DECODE
  //   74HC00   quad 2-input NAND 2 off
  //   74HC10  triple 3-input NAND 2 off
  //   74HC20   dual 4-input NAND 1 off
  //   74HC04   1off  hex inverter   1 off		
  //   74HC02   Quad 2-input NOR 2 off
  //   74HC27   Triple 3-input NOR
  //   8 x 14 pin DIL packages
  //   284
  //   196
  //   350
  //   232
  //   384
  //   256
  //   382
  //   380
  //   372
  //   374
  //   SELECTOR
  //   206
  //   292
  //   262
  //   264
  //   204
  //   288
  //   198
  //   344
  //   214
  //   318
  //   348
  //   290
  //   200
  //   342
  //   TIMING
  //   AMPCR
  //   74HC00   quad 2-input NAND 1off
  //   74HC10  triple 3-input NAND 2 off
  //   74HC20   dual 4-input NAND 0 off
  //   74HC04   1off  hex inverter   1off		
  //   74HC02   Quad 2-input NOR 1off
  //   74HC27   Triple 3-input NOR 0 off
  //   5 x 14 pin DIL packages
  //   1 x 16 pin DIL packages
  //   156
  //   132
  //   142
  //   136
  //   266
  //   320
  //   268
  //   MPCR
  //   SELECTORS
  //   X-SELECTOR
  //   DESTN DECODE (254)
  //   SHIFT DECODE (258)
  //   LC-SET-SELECTOR
  //   REGISTERS
  //   6  x 14 pin DIL packages
  //   5 x 16 pin DIL packages
  //   2 x 20 pin DIL packages
  //   ACC 1
  //   SUCCESSOR-SELECTOR (74HC153)
  //   Note ~N11
  //   LC-RESET-SELECTOR
  //   MST
  //   202
  //   74HC00   quad 2-input NAND 1off
  //   74HC10  triple 3-input NAND 9 off
  //   74HC20   dual 4-input NAND 2 off
  //   74HC04   1off  hex inverter   5 off		
  //   74HC02   Quad 2-input NOR 0 off
  //   74HC27   Triple 3-input NOR 0 off
  //   17 x 14 pin DIL packages
  //   0 x 16 pin DIL packages
  //   LST
  //   286
  //   LC1
  //   306
  //   1
  //   2
  //   3
  //   4
  //   ACC 2
  //   316
  //   324
  //   LC2
  //   308
  //   LC3
  //   310
  //   ALU SECTION
  //   Q
  //   ~Q
  //   X1:X0
  //   I2:  I1:  I0
  //   1----1----1
  //   ADDER
  //   ACC 3
  //   FALSE
  //   230
  //   D7--D6--D5--D4--D3--D2--D1--D0
  //   TRUE
  //   224
  //   222
  //   220
  //   SET LC
  //   CONDITION
  //   248
  //   226
  //   354
  //   352
  //   240
  //   242
  //   244
  //   BUS
  //   246
  //   300
  //   260
  //   282
  //   360
  //   302
  //   304
  //   296
  //   278
  //   74HC00   quad 2-input NAND 1off
  //   74HC10  triple 3-input NAND 3 off
  //   74HC20   dual 4-input NAND 4 off
  //   74HC04   hex inverter   2 off		
  //   74HC02   Quad 2-input NOR 1off
  //   74HC27   Triple 3-input NOR  1 off
  //   74HC86   Quad 2-input XOR 1 off
  //   74HC32 Quad 2-input OR 1 off
  //   14  x 14 pin DIL packages
  //   358
  //   356
  //   274
  //   272
  //   270
  //   370
  //   294
  //   276
  //   368
  //   AOV/Carry FF
endmodule
